# Fritzing sketch board (saved by Fritzing 0.9.2b)

parts:
  Matrix_keypad1 = KEYPAD 4x4
  Part1 = Arduino Uno (Rev3)

nets:
  N1: Matrix_keypad1.col1, Part1.D13/SCK
  N2: Matrix_keypad1.col2, Part1.D12/MISO
  N3: Matrix_keypad1.col3, Part1.D11_PWM/MOSI
  N4: Matrix_keypad1.col4, Part1.D10_PWM/SS
  N5: Matrix_keypad1.row1, Part1.D9_PWM
  N6: Matrix_keypad1.row2, Part1.D8
  N7: Matrix_keypad1.row3, Part1.D7
  N8: Matrix_keypad1.row4, Part1.D6_PWM

custom parts:
  KEYPAD 4x4: Matrix keypad 16 buttons, 4 rows x 4 columns
