# Fritzing sketch board (saved by Fritzing 0.9.2b)
breadboards: 1

parts:
  Part1 = Arduino Uno (Rev3)
  LCD1 = LCD screen [part_number=asf]
  Part2 = Thumb Joystick

nets:
  N1: Part1.A0, Part2.HORZ
  N2: Part1.A1, Part2.ZZ
  N3: Part1.D13/SCK, Part2.pieter
  N4: Part1.D0/RX, LCD1.RS
  N5: Part1.D1/TX, LCD1.E
  N6: Part1.D2, LCD1.DB4
  N7: Part1.D3_PWM, LCD1.DB5
  N8: Part1.D4, LCD1.DB6
  N9: Part1.D5_PWM, LCD1.DB7
  5V: Part1.5V, LCD1.VDD, LCD1.LED+
  GND: Part1.GND, LCD1.VSS, LCD1.V0, LCD1.R/W, LCD1.LED-

custom parts:
  Thumb Joystick: Description: This is the breakout board for the thumb joystick. Pins are broken out to a 0.1" header and includes 4 mounting holes in the corners. Dimensions: 1" x 1.25"
