# Fritzing sketch board (saved by Fritzing 0.9.3b)
breadboards: 1

parts:
  Part1 = Arduino Uno (Rev3)
  LCD1 = LCD screen [part_number=asf]

nets:
  N1: Part1.D8, LCD1.DB4
  N2: Part1.D9_PWM, LCD1.DB5
  N3: Part1.D10_PWM/SS, LCD1.DB6
  N4: Part1.D11_PWM/MOSI, LCD1.DB7
  GND: Part1.GND, LCD1.VSS, LCD1.V0, LCD1.R/W, LCD1.LED-
  N5: Part1.D2, LCD1.RS
  N6: Part1.D3_PWM, LCD1.E
  5V: Part1.5V, LCD1.VDD, LCD1.LED+
